// Logisim project Impl.circ as structural Verilog: 4 circuits, main circuit main
module main (
  input  Reset,
  input  [2:0] Numerator,
  input  [2:0] Denominator,
  output [2:0] N,
  output [2:0] N_2
);

  wire clock_1_out, comparator_1_eq, not_1_out, not_2_out, not_3_out, or_1_out,
       shfitmemoryregister_1_lastbit, subtractor_1_bout;
  wire [1:0] counterstopper_1_output;
  wire [2:0] multiplexer_1_out, register_1_q, subtractor_1_out;

  Register #(.width(3)) register_1 (.D(Denominator), .Q(register_1_q), .clk(clock_1_out));  // open: en, clr
  Clock clock_1 (.out(clock_1_out));
  ShfitMemoryRegister shfitmemoryregister_1 (
    .Clk(clock_1_out), .Input(Numerator), .LastBit(shfitmemoryregister_1_lastbit), .Reset(Reset), .Number(N),
    .Enable(or_1_out));
  ShfitMemoryRegister shfitmemoryregister_2 (
    .Clk(clock_1_out), .Input(multiplexer_1_out), .Number(N_2), .Enable(or_1_out));  // open: LastBit, Reset
  not not_1 (not_1_out, subtractor_1_bout);
  Shift_Register #(.length(3)) shift_register_1 (
    .shift(or_1_out), .in(not_1_out), .clk(clock_1_out), .clr(Reset));  // open: out, load, d0, q0, d1, q1, d2, q2
  Subtractor #(.width(3)) subtractor_1 (
    .a(N_2), .b(register_1_q), .out(subtractor_1_out), .bout(subtractor_1_bout));  // open: bin
  Multiplexer multiplexer_1 (
    .in0(shfitmemoryregister_1_lastbit), .in1(Numerator[2]), .out(multiplexer_1_out[0]), .sel(Reset));  // open: en
  and and_1 (multiplexer_1_out[1], subtractor_1_out[0], not_2_out);
  not not_2 (not_2_out, Reset);
  and and_2 (multiplexer_1_out[2], subtractor_1_out[1], not_2_out);
  or or_1 (or_1_out, Reset, not_3_out);
  CounterStopper counterstopper_1 (
    .Enable(or_1_out), .Clock(clock_1_out), .Reset(Reset), .Output(counterstopper_1_output));
  Comparator #(.width(2), .mode("unsigned")) comparator_1 (
    .a(counterstopper_1_output), .b(2'b11), .eq(comparator_1_eq));  // open: gt, lt
  not not_3 (not_3_out, comparator_1_eq);
endmodule

module ShfitMemoryRegister (
  input  Clk,
  input  [2:0] Input,
  input  Reset,
  input  Enable,
  output LastBit,
  output [2:0] Number
);

  D_Flip_Flop d_ff_1 (.clk(Clk), .D(Input[0]), .Q(Number[0]), .en(Enable));  // open: Qn, preset, reset
  FF_DSelective ff_dselective_1 (
    .Clk(Clk), .ResetValue(Input[1]), .Input(Number[0]), .Select(Reset), .Q(Number[1]), .Enable(Enable));
  FF_DSelective ff_dselective_2 (
    .Clk(Clk), .ResetValue(Input[2]), .Input(Number[1]), .Select(Reset), .Q(LastBit), .Enable(Enable));

  assign Number[2] = LastBit;
endmodule

module FF_DSelective (
  input  Clk,
  input  ResetValue,
  input  Input,
  input  Enable,
  input  Select,
  output Q
);

  wire multiplexer_1_out;

  Multiplexer multiplexer_1 (.in0(Input), .in1(ResetValue), .out(multiplexer_1_out), .sel(Select));  // open: en
  D_Flip_Flop d_ff_1 (.clk(Clk), .D(multiplexer_1_out), .Q(Q), .en(Enable));  // open: Qn, preset, reset
endmodule

module CounterStopper (
  input  Enable,
  input  Clock,
  input  Reset,
  output [1:0] Output
);

  wire [1:0] adder_1_out;

  Adder #(.width(2)) adder_1 (.a(Output), .b(2'b01), .out(adder_1_out));  // open: cin, cout
  Register #(.width(2)) register_1 (.D(adder_1_out), .en(Enable), .Q(Output), .clk(Clock), .clr(Reset));
endmodule
