// Logisim project Impl2.circ as structural Verilog: 6 circuits, main circuit Divisore
module Divisore (
  input  Reset,
  input  Clock,
  input  [2:0] Numerator,
  input  [2:0] Denominator,
  output [2:0] out_5,
  output EndOfC,
  output [2:0] Resto,
  output [2:0] Result
);

  wire not_2_out, not_3_out, or_1_out, or_2_out, shiftmemoryregister2_1_lastbit, subtractor_1_bout;
  wire [1:0] counterstopper_1_output;
  wire [2:0] multiplexer_1_out, register_1_q, subtractor_1_out;

  Register #(.width(3)) register_1 (.D(Denominator), .Q(register_1_q), .clk(Clock));  // open: en, clr
  ShfitMemoryRegister shfitmemoryregister_1 (
    .Clk(Clock), .Input(multiplexer_1_out), .Select(or_1_out), .Number(out_5), .Enable(or_2_out));  // open: LastBit
  or or_1 (or_1_out, Result[0], Reset);
  not not_1 (Result[0], subtractor_1_bout);
  Shift_Register #(.length(2)) shift_register_1 (
    .shift(or_2_out), .in(Result[0]), .clk(Clock), .q0(Result[1]), .q1(Result[2]));  // open: out, load, clr, d0, d1
  ShiftMemoryRegister2 shiftmemoryregister2_1 (
    .Clk(Clock), .Input(Numerator[1:0]), .Select(Reset), .Enable(or_2_out),
    .LastBit(shiftmemoryregister2_1_lastbit));  // open: Number
  Subtractor #(.width(3)) subtractor_1 (
    .a(out_5), .b(register_1_q), .out(subtractor_1_out), .bout(subtractor_1_bout));  // open: bin
  Multiplexer multiplexer_1 (
    .in0(shiftmemoryregister2_1_lastbit), .in1(Numerator[2]), .out(multiplexer_1_out[0]), .sel(Reset));  // open: en
  Multiplexer #(.width(3)) multiplexer_2 (
    .in0(out_5), .in1(subtractor_1_out), .out(Resto), .sel(Result[0]));  // open: en
  and and_1 (multiplexer_1_out[1], subtractor_1_out[0], not_2_out);
  not not_2 (not_2_out, Reset);
  and and_2 (multiplexer_1_out[2], subtractor_1_out[1], not_2_out);
  or or_2 (or_2_out, Reset, not_3_out);
  CounterStopper counterstopper_1 (.Enable(or_2_out), .Clock(Clock), .Reset(Reset), .Output(counterstopper_1_output));
  Comparator #(.width(2), .mode("unsigned")) comparator_1 (
    .a(counterstopper_1_output), .b(2'b10), .eq(EndOfC));  // open: gt, lt
  not not_3 (not_3_out, EndOfC);
endmodule

module ShfitMemoryRegister (
  input  Clk,
  input  [2:0] Input,
  input  Select,
  input  Enable,
  output LastBit,
  output [2:0] Number
);

  D_Flip_Flop d_ff_1 (.clk(Clk), .D(Input[0]), .Q(Number[0]), .en(Enable));  // open: Qn, preset, reset
  FF_DSelective ff_dselective_1 (
    .Clk(Clk), .ResetValue(Input[1]), .Input(Number[0]), .Select(Select), .Q(Number[1]), .Enable(Enable));
  FF_DSelective ff_dselective_2 (
    .Clk(Clk), .ResetValue(Input[2]), .Input(Number[1]), .Select(Select), .Q(LastBit), .Enable(Enable));

  assign Number[2] = LastBit;
endmodule

module FF_DSelective (
  input  Clk,
  input  ResetValue,
  input  Input,
  input  Enable,
  input  Select,
  output Q
);

  wire multiplexer_1_out;

  Multiplexer multiplexer_1 (.in0(Input), .in1(ResetValue), .out(multiplexer_1_out), .sel(Select));  // open: en
  D_Flip_Flop d_ff_1 (.clk(Clk), .D(multiplexer_1_out), .Q(Q), .en(Enable));  // open: Qn, preset, reset
endmodule

module CounterStopper (
  input  Enable,
  input  Clock,
  input  Reset,
  output [1:0] Output
);

  wire [1:0] adder_1_out;

  Adder #(.width(2)) adder_1 (.a(Output), .b(2'b01), .out(adder_1_out));  // open: cin, cout
  Register #(.width(2)) register_1 (.D(adder_1_out), .en(Enable), .Q(Output), .clk(Clock), .clr(Reset));
endmodule

module ShiftMemoryRegister2 (
  input  Clk,
  input  [1:0] Input,
  input  Select,
  input  Enable,
  output LastBit,
  output [1:0] Number
);

  D_Flip_Flop d_ff_1 (.clk(Clk), .D(Input[0]), .Q(Number[0]), .en(Enable));  // open: Qn, preset, reset
  FF_DSelective ff_dselective_1 (
    .Clk(Clk), .ResetValue(Input[1]), .Input(Number[0]), .Select(Select), .Q(LastBit), .Enable(Enable));

  assign Number[1] = LastBit;
endmodule

module Main (
  input  Reset,
  input  [2:0] Numeratore,
  input  [2:0] Denominatore,
  output [2:0] Resto,
  output [2:0] Risultato
);

  wire clock_1_out, divisore_1_endofc;

  Clock clock_1 (.out(clock_1_out));
  LED led_1 (.in(divisore_1_endofc));
  Divisore divisore_1 (
    .Numerator(Numeratore), .Denominator(Denominatore), .Resto(Resto), .Result(Risultato), .Reset(Reset),
    .EndOfC(divisore_1_endofc), .Clock(clock_1_out));  // open: out_5
endmodule
