// Logisim project Prova.circ as structural Verilog: 1 circuit, main circuit main
module main (
  input  [2:0] N,
  input  [2:0] D,
  input  RST,
  output [2:0] out_4
);

  wire and_1_out, and_2_out, and_3_out, clock_1_out, d_ff_1_q, d_ff_3_q, d_ff_5_q, d_ff_7_q,
       multiplexer_1_out, multiplexer_2_out, multiplexer_3_out, multiplexer_4_out, not_1_out, not_2_out,
       or_1_out, subtractor_1_bout;
  wire [2:0] d_ff_2_q;

  Clock #(.highDuration(10), .lowDuration(10)) clock_1 (.out(clock_1_out));
  Multiplexer multiplexer_1 (.in0(d_ff_5_q), .in1(N[0]), .out(multiplexer_1_out), .sel(RST));  // open: en
  D_Flip_Flop d_ff_1 (.clk(clock_1_out), .D(multiplexer_1_out), .Q(d_ff_1_q));  // open: Qn, preset, en, reset
  D_Flip_Flop d_ff_2 (.clk(clock_1_out), .D(d_ff_5_q), .Q(d_ff_2_q[0]));  // open: Qn, preset, en, reset
  Multiplexer multiplexer_2 (.in0(d_ff_1_q), .in1(N[1]), .out(multiplexer_2_out), .sel(RST));  // open: en
  Multiplexer multiplexer_3 (.in0(and_3_out), .in1(d_ff_2_q[0]), .out(multiplexer_3_out), .sel(and_1_out));  // open: en
  Subtractor #(.width(3)) subtractor_1 (.a(d_ff_2_q), .b(D), .out(out_4), .bout(subtractor_1_bout));  // open: bin
  not not_1 (not_1_out, subtractor_1_bout);
  D_Flip_Flop d_ff_3 (.clk(clock_1_out), .D(multiplexer_2_out), .Q(d_ff_3_q));  // open: Qn, preset, en, reset
  D_Flip_Flop d_ff_4 (.clk(clock_1_out), .D(multiplexer_3_out), .Q(d_ff_2_q[1]));  // open: Qn, preset, en, reset
  and and_1 (and_1_out, subtractor_1_bout, not_2_out);
  Shift_Register #(.length(3)) shift_register_1 (
    .in(not_1_out), .clk(clock_1_out), .clr(or_1_out));  // open: shift, out, load, d0, q0, d1, q1, d2, q2
  Multiplexer multiplexer_4 (.in0(d_ff_3_q), .in1(N[2]), .out(multiplexer_4_out), .sel(RST));  // open: en
  D_Flip_Flop d_ff_5 (.clk(clock_1_out), .D(multiplexer_4_out), .Q(d_ff_5_q));  // open: Qn, preset, en, reset
  Multiplexer multiplexer_5 (.in0(and_2_out), .in1(d_ff_2_q[1]), .sel(and_1_out));  // open: out, en
  D_Flip_Flop d_ff_6 (.clk(clock_1_out), .Q(d_ff_2_q[2]));  // open: D, Qn, preset, en, reset
  and and_2 (and_2_out, not_2_out, out_4[1]);
  and and_3 (and_3_out, out_4[0], not_2_out);
  or or_1 (or_1_out, RST, d_ff_7_q);
  D_Flip_Flop d_ff_7 (.clk(clock_1_out), .D(RST), .Q(d_ff_7_q));  // open: Qn, preset, en, reset
  not not_2 (not_2_out, d_ff_7_q);

  // Notes on the sheet:
  //   out_4: pull=up
endmodule
